// Logisim project circuit1c.circ as structural Verilog: 1 circuit, main circuit main
module main (
  input  C,
  input  B,
  input  A,
  output out1,
  output out2
);

  wire and_1_out, and_2_out, and_3_out, and_4_out, not_1_out, not_2_out, not_3_out, not_4_out, not_5_out;

  not not_1 (not_1_out, A);
  not not_2 (not_2_out, A);
  not not_3 (not_3_out, C);
  not not_4 (not_4_out, B);
  and and_1 (and_1_out, not_1_out, B);
  and and_2 (and_2_out, not_2_out, not_3_out);
  and and_3 (and_3_out, A, not_4_out, C);
  not not_5 (not_5_out, A);
  and and_4 (and_4_out, not_5_out, C);
  or or_1 (out1, and_1_out, and_2_out, and_3_out);
  or or_2 (out2, B, and_4_out);
endmodule
