// Logisim project my_adder.circ as structural Verilog: 2 circuits, main circuit main
module main (
  input  [15:0] B,
  input  [15:0] A,
  input  sub,
  output [15:0] result,
  output ovf
);

  wire adderbit_1_cout, adderbit_2_cout, adderbit_3_cout, adderbit_4_cout, adderbit_5_cout, adderbit_6_cout,
       adderbit_7_cout, adderbit_8_cout, adderbit_9_cout, adderbit_10_cout, adderbit_11_cout,
       adderbit_12_cout, adderbit_13_cout, adderbit_14_cout, adderbit_15_cout, adderbit_16_cout, xor_1_out,
       xor_2_out, xor_3_out, xor_4_out, xor_5_out, xor_6_out, xor_7_out, xor_8_out, xor_9_out, xor_10_out,
       xor_11_out, xor_12_out, xor_13_out, xor_14_out, xor_15_out, xor_16_out;

  xor xor_1 (xor_1_out, sub, B[15]);
  xor xor_2 (xor_2_out, sub, B[14]);
  xor xor_3 (xor_3_out, sub, B[13]);
  xor xor_4 (xor_4_out, sub, B[12]);
  xor xor_5 (xor_5_out, sub, B[11]);
  xor xor_6 (xor_6_out, sub, B[10]);
  xor xor_7 (xor_7_out, sub, B[9]);
  xor xor_8 (xor_8_out, sub, B[8]);
  xor xor_9 (xor_9_out, sub, B[7]);
  xor xor_10 (xor_10_out, sub, B[6]);
  xor xor_11 (xor_11_out, sub, B[5]);
  xor xor_12 (xor_12_out, sub, B[4]);
  xor xor_13 (xor_13_out, sub, B[3]);
  xor xor_14 (xor_14_out, sub, B[2]);
  xor xor_15 (xor_15_out, sub, B[1]);
  xor xor_16 (xor_16_out, sub, B[0]);
  adderbit adderbit_1 (.Cout(adderbit_1_cout), .Cin(adderbit_2_cout), .Sum(result[15]), .A(A[15]), .B(xor_1_out));
  adderbit adderbit_2 (.Cout(adderbit_2_cout), .Cin(adderbit_3_cout), .Sum(result[14]), .A(A[14]), .B(xor_2_out));
  adderbit adderbit_3 (.Cout(adderbit_3_cout), .Cin(adderbit_4_cout), .Sum(result[13]), .A(A[13]), .B(xor_3_out));
  adderbit adderbit_4 (.Cout(adderbit_4_cout), .Cin(adderbit_5_cout), .Sum(result[12]), .A(A[12]), .B(xor_4_out));
  adderbit adderbit_5 (.Cout(adderbit_5_cout), .Cin(adderbit_6_cout), .Sum(result[11]), .A(A[11]), .B(xor_5_out));
  adderbit adderbit_6 (.Cout(adderbit_6_cout), .Cin(adderbit_7_cout), .Sum(result[10]), .A(A[10]), .B(xor_6_out));
  adderbit adderbit_7 (.Cout(adderbit_7_cout), .Cin(adderbit_8_cout), .Sum(result[9]), .A(A[9]), .B(xor_7_out));
  adderbit adderbit_8 (.Cout(adderbit_8_cout), .Cin(adderbit_9_cout), .Sum(result[8]), .A(A[8]), .B(xor_8_out));
  adderbit adderbit_9 (.Cout(adderbit_9_cout), .Cin(adderbit_10_cout), .Sum(result[7]), .A(A[7]), .B(xor_9_out));
  adderbit adderbit_10 (.Cout(adderbit_10_cout), .Cin(adderbit_11_cout), .Sum(result[6]), .A(A[6]), .B(xor_10_out));
  adderbit adderbit_11 (.Cout(adderbit_11_cout), .Cin(adderbit_12_cout), .Sum(result[5]), .A(A[5]), .B(xor_11_out));
  adderbit adderbit_12 (.Cout(adderbit_12_cout), .Cin(adderbit_13_cout), .Sum(result[4]), .A(A[4]), .B(xor_12_out));
  adderbit adderbit_13 (.Cout(adderbit_13_cout), .Cin(adderbit_14_cout), .Sum(result[3]), .A(A[3]), .B(xor_13_out));
  adderbit adderbit_14 (.Cout(adderbit_14_cout), .Cin(adderbit_15_cout), .Sum(result[2]), .A(A[2]), .B(xor_14_out));
  adderbit adderbit_15 (.Cout(adderbit_15_cout), .Cin(adderbit_16_cout), .Sum(result[1]), .A(A[1]), .B(xor_15_out));
  adderbit adderbit_16 (.Cout(adderbit_16_cout), .Cin(sub), .Sum(result[0]), .A(A[0]), .B(xor_16_out));
  xor xor_17 (ovf, adderbit_2_cout, adderbit_1_cout);
endmodule

module adderbit (
  input  Cin,
  input  A,
  input  B,
  output Sum,
  output Cout
);

  wire and_1_out, and_2_out, xor_1_out;

  xor xor_1 (xor_1_out, A, B);
  and and_1 (and_1_out, A, B);
  and and_2 (and_2_out, xor_1_out, Cin);
  or or_1 (Cout, and_2_out, and_1_out);
  xor xor_2 (Sum, Cin, xor_1_out);
endmodule
