// Logisim project my_adderM.circ as structural Verilog: 2 circuits, main circuit main
module main (
  input  sub,
  input  [15:0] B,
  input  [15:0] A,
  output [15:0] result,
  output ovf
);

  wire bitfulladder_1_c_out, bitfulladder_2_c_out, bitfulladder_3_c_out, bitfulladder_4_c_out,
       bitfulladder_5_c_out, bitfulladder_6_c_out, bitfulladder_7_c_out, bitfulladder_8_c_out,
       bitfulladder_9_c_out, bitfulladder_10_c_out, bitfulladder_11_c_out, bitfulladder_12_c_out,
       bitfulladder_13_c_out, bitfulladder_14_c_out, bitfulladder_15_c_out, bitfulladder_16_c_out, xor_2_out,
       xor_3_out, xor_4_out, xor_5_out, xor_6_out, xor_7_out, xor_8_out, xor_9_out, xor_10_out, xor_11_out,
       xor_12_out, xor_13_out, xor_14_out, xor_15_out, xor_16_out, xor_17_out;

  xor xor_1 (ovf, bitfulladder_1_c_out, bitfulladder_2_c_out);
  bitFullAdder bitfulladder_1 (
    .a(xor_2_out), .b(A[15]), .sum(result[15]), .c_in(bitfulladder_2_c_out), .c_out(bitfulladder_1_c_out));
  xor xor_2 (xor_2_out, sub, B[15]);
  bitFullAdder bitfulladder_2 (
    .a(xor_3_out), .b(A[14]), .sum(result[14]), .c_in(bitfulladder_3_c_out), .c_out(bitfulladder_2_c_out));
  xor xor_3 (xor_3_out, sub, B[14]);
  bitFullAdder bitfulladder_3 (
    .a(xor_4_out), .b(A[13]), .sum(result[13]), .c_in(bitfulladder_4_c_out), .c_out(bitfulladder_3_c_out));
  xor xor_4 (xor_4_out, sub, B[13]);
  bitFullAdder bitfulladder_4 (
    .a(xor_5_out), .b(A[12]), .sum(result[12]), .c_in(bitfulladder_5_c_out), .c_out(bitfulladder_4_c_out));
  xor xor_5 (xor_5_out, sub, B[12]);
  bitFullAdder bitfulladder_5 (
    .a(xor_6_out), .b(A[11]), .sum(result[11]), .c_in(bitfulladder_6_c_out), .c_out(bitfulladder_5_c_out));
  xor xor_6 (xor_6_out, sub, B[11]);
  bitFullAdder bitfulladder_6 (
    .a(xor_7_out), .b(A[10]), .sum(result[10]), .c_in(bitfulladder_7_c_out), .c_out(bitfulladder_6_c_out));
  xor xor_7 (xor_7_out, sub, B[10]);
  bitFullAdder bitfulladder_7 (
    .a(xor_8_out), .b(A[9]), .sum(result[9]), .c_in(bitfulladder_8_c_out), .c_out(bitfulladder_7_c_out));
  xor xor_8 (xor_8_out, sub, B[9]);
  bitFullAdder bitfulladder_8 (
    .a(xor_9_out), .b(A[8]), .sum(result[8]), .c_in(bitfulladder_9_c_out), .c_out(bitfulladder_8_c_out));
  xor xor_9 (xor_9_out, sub, B[8]);
  bitFullAdder bitfulladder_9 (
    .a(xor_10_out), .b(A[7]), .sum(result[7]), .c_in(bitfulladder_10_c_out), .c_out(bitfulladder_9_c_out));
  xor xor_10 (xor_10_out, sub, B[7]);
  bitFullAdder bitfulladder_10 (
    .a(xor_11_out), .b(A[6]), .sum(result[6]), .c_in(bitfulladder_11_c_out), .c_out(bitfulladder_10_c_out));
  xor xor_11 (xor_11_out, sub, B[6]);
  bitFullAdder bitfulladder_11 (
    .a(xor_12_out), .b(A[5]), .sum(result[5]), .c_in(bitfulladder_12_c_out), .c_out(bitfulladder_11_c_out));
  xor xor_12 (xor_12_out, sub, B[5]);
  bitFullAdder bitfulladder_12 (
    .a(xor_13_out), .b(A[4]), .sum(result[4]), .c_in(bitfulladder_13_c_out), .c_out(bitfulladder_12_c_out));
  xor xor_13 (xor_13_out, sub, B[4]);
  bitFullAdder bitfulladder_13 (
    .a(xor_14_out), .b(A[3]), .sum(result[3]), .c_in(bitfulladder_14_c_out), .c_out(bitfulladder_13_c_out));
  xor xor_14 (xor_14_out, sub, B[3]);
  bitFullAdder bitfulladder_14 (
    .a(xor_15_out), .b(A[2]), .sum(result[2]), .c_in(bitfulladder_15_c_out), .c_out(bitfulladder_14_c_out));
  xor xor_15 (xor_15_out, sub, B[2]);
  bitFullAdder bitfulladder_15 (
    .a(xor_16_out), .b(A[1]), .sum(result[1]), .c_in(bitfulladder_16_c_out), .c_out(bitfulladder_15_c_out));
  xor xor_16 (xor_16_out, sub, B[1]);
  bitFullAdder bitfulladder_16 (.a(xor_17_out), .b(A[0]), .sum(result[0]), .c_in(sub), .c_out(bitfulladder_16_c_out));
  xor xor_17 (xor_17_out, sub, B[0]);

  // Other names for the same wires on the sheet: a_t[15:0] = A; b_t[15:0] = B
endmodule

module bitFullAdder (
  input  c_in,
  input  a,
  input  b,
  output sum,
  output c_out
);

  wire and_1_out, and_2_out, xor_1_out;

  and and_1 (and_1_out, b, a);
  or or_1 (c_out, and_1_out, and_2_out);
  xor xor_1 (xor_1_out, a, b);
  and and_2 (and_2_out, xor_1_out, c_in);
  xor xor_2 (sum, c_in, xor_1_out);
endmodule
