// Logisim project vending.circ as structural Verilog: 1 circuit, main circuit main
module main (
  input  D,
  input  N,
  input  RESET,
  output DISPENSE,
  output DOH,
  output DESPERATE
);

  wire A, and_1_out, and_2_out, and_3_out, and_4_out, and_5_out, and_6_out, and_7_out, and_8_out, and_9_out,
       and_10_out, and_11_out, and_12_out, and_13_out, and_14_out, and_15_out, and_16_out, and_17_out,
       and_18_out, and_19_out, and_20_out, and_21_out, and_22_out, and_23_out, and_25_out, and_26_out, B, C,
       clk, not_1_out, not_2_out, not_3_out, not_4_out, not_5_out, not_6_out, not_7_out, not_8_out,
       not_9_out, not_10_out, not_11_out, not_12_out, not_13_out, not_14_out, not_15_out, not_16_out,
       not_17_out, not_18_out, not_19_out, not_20_out, not_21_out, not_22_out, not_23_out, not_24_out,
       not_25_out, not_26_out, not_27_out, not_28_out, not_29_out, not_30_out, not_31_out, not_32_out,
       not_33_out, not_34_out, not_35_out, not_36_out, not_37_out, not_38_out, not_39_out, not_40_out,
       not_41_out, not_42_out, not_43_out, not_44_out, not_45_out, not_46_out, not_47_out, not_48_out,
       not_49_out, not_50_out, not_51_out, not_52_out, not_53_out, not_54_out, not_55_out, not_56_out,
       not_57_out, not_58_out, not_59_out, not_60_out, not_61_out, not_62_out, not_63_out, not_64_out,
       not_65_out, or_1_out, or_2_out, or_3_out;

  Clock clock_1 (.out(clk));
  not not_1 (not_1_out, D);
  not not_2 (not_2_out, A);
  not not_3 (not_3_out, N);
  not not_4 (not_4_out, A);
  not not_5 (not_5_out, N);
  not not_6 (not_6_out, D);
  not not_7 (not_7_out, B);
  not not_8 (not_8_out, D);
  not not_9 (not_9_out, B);
  not not_10 (not_10_out, N);
  not not_11 (not_11_out, B);
  not not_12 (not_12_out, RESET);
  not not_13 (not_13_out, C);
  not not_14 (not_14_out, B);
  not not_15 (not_15_out, D);
  not not_16 (not_16_out, B);
  not not_17 (not_17_out, A);
  not not_18 (not_18_out, D);
  not not_19 (not_19_out, C);
  not not_20 (not_20_out, B);
  not not_21 (not_21_out, A);
  not not_22 (not_22_out, N);
  not not_23 (not_23_out, D);
  not not_24 (not_24_out, A);
  not not_25 (not_25_out, N);
  not not_26 (not_26_out, B);
  not not_27 (not_27_out, RESET);
  not not_28 (not_28_out, C);
  not not_29 (not_29_out, N);
  not not_30 (not_30_out, B);
  not not_31 (not_31_out, A);
  not not_32 (not_32_out, RESET);
  not not_33 (not_33_out, C);
  not not_34 (not_34_out, A);
  not not_35 (not_35_out, D);
  not not_36 (not_36_out, C);
  not not_37 (not_37_out, B);
  not not_38 (not_38_out, A);
  not not_39 (not_39_out, N);
  not not_40 (not_40_out, C);
  not not_41 (not_41_out, B);
  not not_42 (not_42_out, A);
  not not_43 (not_43_out, N);
  not not_44 (not_44_out, D);
  not not_45 (not_45_out, A);
  not not_46 (not_46_out, D);
  not not_47 (not_47_out, A);
  not not_48 (not_48_out, N);
  not not_49 (not_49_out, D);
  not not_50 (not_50_out, B);
  not not_51 (not_51_out, N);
  not not_52 (not_52_out, D);
  not not_53 (not_53_out, B);
  not not_54 (not_54_out, A);
  and and_1 (and_1_out, N, not_1_out, C, B, not_2_out);
  and and_2 (and_2_out, not_3_out, D, C, B, not_4_out);
  and and_3 (and_3_out, not_5_out, not_6_out, C, not_7_out, A);
  and and_4 (and_4_out, N, not_8_out, C, not_9_out, A);
  and and_5 (and_5_out, not_10_out, D, C, not_11_out, A);
  not not_55 (not_55_out, RESET);
  not not_56 (not_56_out, C);
  and and_6 (and_6_out, not_55_out, not_56_out, B, A);
  and and_7 (and_7_out, not_12_out, not_13_out, not_14_out, A);
  and and_8 (and_8_out, N, not_15_out, C, not_16_out, not_17_out);
  and and_9 (and_9_out, N, not_18_out, not_19_out, not_20_out, not_21_out);
  and and_10 (and_10_out, not_22_out, not_23_out, C, B, not_24_out);
  and and_11 (and_11_out, not_25_out, D, C, not_26_out, A);
  and and_12 (and_12_out, not_27_out, not_28_out, B, A);
  and and_13 (and_13_out, not_29_out, D, C, not_30_out, not_31_out);
  and and_14 (and_14_out, not_32_out, not_33_out, B, not_34_out);
  and and_15 (and_15_out, N, not_35_out, not_36_out, not_37_out, not_38_out);
  and and_16 (and_16_out, not_39_out, D, not_40_out, not_41_out, not_42_out);
  and and_17 (and_17_out, not_43_out, not_44_out, C, B, not_45_out);
  and and_18 (and_18_out, N, not_46_out, C, B, not_47_out);
  and and_19 (and_19_out, not_48_out, not_49_out, C, not_50_out, A);
  and and_20 (and_20_out, not_51_out, not_52_out, C, not_53_out, not_54_out);
  D_Flip_Flop d2 (.D(or_1_out), .clk(clk), .Q(A));  // open: Qn, preset, reset
  or or_1 (or_1_out, and_1_out, and_2_out, and_3_out, and_4_out, and_5_out, and_6_out, and_7_out, and_8_out);
  D_Flip_Flop d1 (.D(or_2_out), .clk(clk), .Q(B));  // open: Qn, preset, reset
  or or_2 (or_2_out, and_9_out, and_10_out, and_11_out, and_12_out, and_13_out, and_14_out);
  D_Flip_Flop d0 (.D(or_3_out), .clk(clk), .Q(C));  // open: Qn, preset, reset
  or or_3 (or_3_out, and_15_out, and_16_out, and_17_out, and_18_out, and_19_out, and_20_out);
  not not_57 (not_57_out, C);
  and and_21 (and_21_out, not_57_out, B, not_58_out);
  not not_58 (not_58_out, A);
  not not_59 (not_59_out, C);
  and and_22 (and_22_out, not_59_out, not_60_out, A);
  not not_60 (not_60_out, B);
  not not_61 (not_61_out, C);
  and and_23 (and_23_out, not_61_out, B, A);
  not not_62 (not_62_out, C);
  and and_24 (DOH, not_62_out, B, A);
  not not_63 (not_63_out, C);
  and and_25 (and_25_out, not_63_out, B, not_64_out);
  not not_64 (not_64_out, A);
  not not_65 (not_65_out, C);
  and and_26 (and_26_out, not_65_out, B, A);
  or or_4 (DISPENSE, and_21_out, and_22_out, and_23_out);
  or or_5 (DESPERATE, and_25_out, and_26_out);

  // Notes on the sheet:
  //   NND - 20.
  //   - 3 Cases:
  //   1) DD - 20;
  //   2) ND - 15;
  //   3) NND - 20;
  //   - 2 Cases:
  //   1) DD - 20;
  //   2) NND - 20;
endmodule
