// Logisim project cpu.circ as structural Verilog: 10 circuits, main circuit main
module main (
  input  reset
);

  wire alu_3_zero, ALUinB, and_1_out, and_2_out, and_3_out, BLE, BNE, clk, DMwe, INPT, JAL, JMP, JR,
       keyboard_1_avail, memorylatch_1_oe_latched, memorylatch_1_we_latched, not_1_out, not_2_out, not_3_out,
       or_1_out, or_2_out, OUTPT, Rdst, RwD, RWe;
  wire [2:0] ALUOp, multiplexer_3_out, multiplexer_4_out;
  wire [3:0] shmtxx;
  wire [7:0] clavier_dordinateur;
  wire [11:0] address;
  wire [15:0] alu_1_outputdata, alu_2_outputdata, alu_3_lteq, alu_3_outputdata,
       memorylatch_1_address_latched, memorylatch_1_data_in_latched, multiplexer_1_out, multiplexer_2_out,
       multiplexer_5_out, multiplexer_6_out, multiplexer_7_out, multiplexer_8_out, multiplexer_9_out,
       oneregister_1_out_16, ram_1_dout, RFrd1, RFrd2, sgnxtImm, xaddress;
  wire [15:12] InsMem;

  Clock clock_1 (.out(clk));
  Multiplexer #(.width(16), .enable("false")) multiplexer_1 (
    .in0(multiplexer_6_out), .in1(RFrd1), .out(multiplexer_1_out), .sel(JR));
  not not_1 (not_1_out, clk);
  oneregister oneregister_1 (
    .out_16(oneregister_1_out_16), .reset(reset), .writeEnable(1'b1), .clk(not_1_out),
    .or_In(multiplexer_1_out));
  ROM #(.addrWidth(16), .dataWidth(16)) InsertionMemory (.addr(oneregister_1_out_16), .data({InsMem, address}));
  InstrDecoder instrdecoder_1 (
    .BNE(BNE), .BLE(BLE), .DMwe(DMwe), .Rdst(Rdst), .opcode(InsMem), .ALUinB(ALUinB), .RwD(RwD), .RWe(RWe),
    .JAL(JAL), .JMP(JMP), .inpt(INPT), .outpt(OUTPT), .ALUOp(ALUOp), .JR(JR));
  assign sgnxtImm = {{10{address[5]}}, address[5:0]};  // Bit_Extender bit_extender_1
  assign xaddress = {{4{address[11]}}, address};  // Bit_Extender bit_extender_2
  // Probe on sgnxtImm
  // Probe on ALUOp
  // Probe on InsMem
  // Probe on address[2:0]
  // Probe on address[5:3]
  // Probe on address[8:6]
  // Probe on address[11:9]
  ALU alu_1 (
    .OpType(3'b000), .InputData2(16'h1), .InputData1(oneregister_1_out_16), .OutputData(alu_1_outputdata));  // open: shift, zero, lteq
  not not_2 (not_2_out, alu_3_zero);
  and and_1 (and_1_out, BNE, alu_3_zero);
  and and_2 (and_2_out, BLE, not_2_out);
  and and_3 (and_3_out, BLE, alu_3_lteq[15]);
  assign shmtxx = {{1{1'b0}}, address[2:0]};  // Bit_Extender bit_extender_3
  Multiplexer #(.width(16), .enable("false")) multiplexer_2 (
    .in0(multiplexer_8_out), .in1(alu_1_outputdata), .out(multiplexer_2_out), .sel(JAL));
  Multiplexer #(.width(3), .enable("false")) multiplexer_3 (
    .in0(address[8:6]), .in1(address[5:3]), .out(multiplexer_3_out), .sel(Rdst));
  ALU alu_2 (
    .OpType(3'b000), .InputData2(sgnxtImm), .InputData1(alu_1_outputdata), .OutputData(alu_2_outputdata));  // open: shift, zero, lteq
  or or_1 (or_1_out, and_1_out, or_2_out);
  or or_2 (or_2_out, and_2_out, and_3_out);
  Multiplexer #(.width(3), .enable("false")) multiplexer_4 (
    .in0(multiplexer_3_out), .in1(3'b111), .out(multiplexer_4_out), .sel(JAL));
  Multiplexer #(.width(16), .enable("false")) multiplexer_5 (
    .in0(alu_1_outputdata), .in1(alu_2_outputdata), .out(multiplexer_5_out), .sel(or_1_out));
  RegisterFile registerfile_1 (
    .ReadRegister1(address[11:9]), .WriteReg(multiplexer_4_out), .reset(reset), .RegWriteEnable(RWe),
    .clk(clk), .ReadRegister2(address[8:6]), .DataInput(multiplexer_2_out), .ReadingD1(RFrd1),
    .ReadingD2(RFrd2));
  Multiplexer #(.width(16), .enable("false")) multiplexer_6 (
    .in0(multiplexer_5_out), .in1(xaddress), .out(multiplexer_6_out), .sel(JMP));
  Multiplexer #(.width(16), .enable("false")) multiplexer_7 (
    .in0(RFrd2), .in1(sgnxtImm), .out(multiplexer_7_out), .sel(ALUinB));
  ALU alu_3 (
    .OpType(ALUOp), .InputData2(multiplexer_7_out), .InputData1(RFrd1), .shift(shmtxx),
    .OutputData(alu_3_outputdata), .zero(alu_3_zero), .lteq(alu_3_lteq));
  TTY #(.rows(13), .cols(80)) tty_1 (.data(RFrd1[6:0]), .clk(clk), .we(OUTPT), .clr(reset));
  Keyboard keyboard_1 (.clk(clk), .re(INPT), .clr(reset), .avail(keyboard_1_avail), .data(clavier_dordinateur[6:0]));
  not not_3 (not_3_out, clk);
  memorylatch memorylatch_1 (
    .address(alu_3_outputdata), .WE(DMwe), .clk(not_3_out), .data_in(RFrd2),
    .address_latched(memorylatch_1_address_latched), .WE_latched(memorylatch_1_we_latched),
    .OE_latched(memorylatch_1_oe_latched), .data_in_latched(memorylatch_1_data_in_latched));
  not not_4 (clavier_dordinateur[7], keyboard_1_avail);
  RAM #(.addrWidth(16), .dataWidth(16), .trigger("high"), .databus("bibus")) ram_1 (
    .addr(memorylatch_1_address_latched), .we(memorylatch_1_we_latched), .oe(memorylatch_1_oe_latched),
    .din(memorylatch_1_data_in_latched), .dout(ram_1_dout));
  Multiplexer #(.width(16), .enable("false")) multiplexer_8 (
    .in0(multiplexer_9_out), .in1({{8{1'b0}}, clavier_dordinateur}), .out(multiplexer_8_out), .sel(INPT));
  Multiplexer #(.width(16), .enable("false")) multiplexer_9 (
    .in0(alu_3_outputdata), .in1(ram_1_dout), .out(multiplexer_9_out), .sel(RwD));

  // Other names for the same wires on the sheet: InsMem[11:0] = address; lmm[5:0] = address[5:0];
  //   Shamt[2:0] = address[2:0]; Rd[2:0] = address[5:3]; Rt[2:0] = address[8:6]; Rs[2:0] = address[11:9];
  //   OpCode[3:0] = InsMem

  // Notes on the sheet:
  //   j Type
  //   r
  //   R type
  //   I- type
endmodule

module InstrDecoder (
  input  [3:0] opcode,
  output ALUinB,
  output Rdst,
  output DMwe,
  output RwD,
  output BLE,
  output BNE,
  output JAL,
  output RWe,
  output JMP,
  output inpt,
  output outpt,
  output JR,
  output [2:0] ALUOp
);

  wire add, addi, and_i, j, not_i, sll_i, srl_i, sub;

  Decoder #(.select(4), .enable("false")) decoder_1 (
    .out0(add), .out1(addi), .out2(sub), .out3(sll_i), .out4(srl_i), .out5(and_i), .out6(not_i), .out7(RwD),
    .out8(DMwe), .out9(BNE), .out10(BLE), .out11(j), .out12(JR), .out13(JAL), .out14(inpt), .out15(outpt),
    .sel(opcode));
  or or_1 (ALUOp[2], and_i, not_i);
  or or_2 (ALUOp[1], srl_i, sll_i);
  or or_3 (ALUOp[0], srl_i, and_i, sub);
  or or_4 (Rdst, add, sub, sll_i, srl_i, and_i, not_i, JR);
  or or_5 (RWe, inpt, add, addi, sub, sll_i, srl_i, and_i, RwD, not_i, JAL);
  or or_6 (ALUinB, RwD, DMwe, addi);
  or or_7 (JMP, j, JAL, JR);

  // Other names for the same wires on the sheet: input_i = inpt; lw = RwD; output_i = outpt; sw = DMwe

  // Notes on the sheet:
  //   add = 000; sub = 001; lsh = 010; rsh = 011; not = 100; AND = 101
endmodule

module RegisterFile (
  input  [15:0] DataInput,
  input  clk,
  input  reset,
  input  [2:0] ReadRegister1,
  input  RegWriteEnable,
  input  [2:0] WriteReg,
  input  [2:0] ReadRegister2,
  output [15:0] ReadingD1,
  output [15:0] ReadingD2
);

  wire read01, read02, read11, read12, read21, read22, read31, read32, read41, read42, read51, read52,
       read61, read62, read71, read72, write0, write1, write2, write3, write4, write5, write6, write7;
  wire [15:0] oneregister_1_out_16, oneregister_2_out_16, oneregister_3_out_16, oneregister_4_out_16,
       reg0_out_16, reg1_out_16, reg2_out_16, reg3_out_16;

  Decoder #(.select(3), .enable("false")) decoder_1 (
    .out0(read01), .out1(read11), .out2(read21), .out3(read31), .out4(read41), .out5(read51), .out6(read61),
    .out7(read71), .sel(ReadRegister1));
  Decoder #(.select(3)) decoder_2 (
    .out0(write0), .out1(write1), .out2(write2), .out3(write3), .out4(write4), .out5(write5), .out6(write6),
    .out7(write7), .sel(WriteReg), .en(RegWriteEnable));
  Decoder #(.select(3), .enable("false")) decoder_3 (
    .out0(read02), .out1(read12), .out2(read22), .out3(read32), .out4(read42), .out5(read52), .out6(read62),
    .out7(read72), .sel(ReadRegister2));
  // Probe on reg1_out_16
  // Probe on reg2_out_16
  // Probe on reg3_out_16
  oneregister reg0 (.out_16(reg0_out_16), .reset(reset), .writeEnable(write0), .clk(clk), .or_In({16{1'b0}}));
  oneregister reg1 (.out_16(reg1_out_16), .reset(reset), .writeEnable(write1), .clk(clk), .or_In(DataInput));
  oneregister reg2 (.out_16(reg2_out_16), .reset(reset), .writeEnable(write2), .clk(clk), .or_In(DataInput));
  oneregister reg3 (.out_16(reg3_out_16), .reset(reset), .writeEnable(write3), .clk(clk), .or_In(DataInput));
  // Probe on reg0_out_16
  assign ReadingD2 = read02 ? reg0_out_16 : 16'bz;  // Controlled_Buffer controlled_buffer_1
  assign ReadingD1 = read01 ? reg0_out_16 : 16'bz;  // Controlled_Buffer controlled_buffer_2
  assign ReadingD2 = read12 ? reg1_out_16 : 16'bz;  // Controlled_Buffer controlled_buffer_3
  assign ReadingD1 = read11 ? reg1_out_16 : 16'bz;  // Controlled_Buffer controlled_buffer_4
  assign ReadingD2 = read22 ? reg2_out_16 : 16'bz;  // Controlled_Buffer controlled_buffer_5
  assign ReadingD1 = read21 ? reg2_out_16 : 16'bz;  // Controlled_Buffer controlled_buffer_6
  assign ReadingD2 = read32 ? reg3_out_16 : 16'bz;  // Controlled_Buffer controlled_buffer_7
  assign ReadingD1 = read31 ? reg3_out_16 : 16'bz;  // Controlled_Buffer controlled_buffer_8
  // Probe on oneregister_1_out_16
  oneregister oneregister_1 (
    .out_16(oneregister_1_out_16), .reset(reset), .writeEnable(write4), .clk(clk), .or_In(DataInput));
  oneregister oneregister_2 (
    .out_16(oneregister_2_out_16), .reset(reset), .writeEnable(write5), .clk(clk), .or_In(DataInput));
  oneregister oneregister_3 (
    .out_16(oneregister_3_out_16), .reset(reset), .writeEnable(write6), .clk(clk), .or_In(DataInput));
  oneregister oneregister_4 (
    .out_16(oneregister_4_out_16), .reset(reset), .writeEnable(write7), .clk(clk), .or_In(DataInput));
  assign ReadingD2 = read42 ? oneregister_1_out_16 : 16'bz;  // Controlled_Buffer controlled_buffer_9
  assign ReadingD1 = read41 ? oneregister_1_out_16 : 16'bz;  // Controlled_Buffer controlled_buffer_10
  assign ReadingD2 = read52 ? oneregister_2_out_16 : 16'bz;  // Controlled_Buffer controlled_buffer_11
  assign ReadingD1 = read51 ? oneregister_2_out_16 : 16'bz;  // Controlled_Buffer controlled_buffer_12
  assign ReadingD2 = read62 ? oneregister_3_out_16 : 16'bz;  // Controlled_Buffer controlled_buffer_13
  assign ReadingD1 = read61 ? oneregister_3_out_16 : 16'bz;  // Controlled_Buffer controlled_buffer_14
  assign ReadingD2 = read72 ? oneregister_4_out_16 : 16'bz;  // Controlled_Buffer controlled_buffer_15
  assign ReadingD1 = read71 ? oneregister_4_out_16 : 16'bz;  // Controlled_Buffer controlled_buffer_16
  // Probe on oneregister_2_out_16
  // Probe on oneregister_3_out_16
  // Probe on oneregister_4_out_16

  // Other names for the same wires on the sheet: clk_rf = clk; data_in[15:0] = DataInput; regwe = RegWriteEnable;
  //   reset_rf = reset
endmodule

module oneregister (
  input  writeEnable,
  input  clk,
  input  reset,
  input  [15:0] or_In,
  output [15:0] out_16
);

  wire clk_t;

  and and_1 (clk_t, writeEnable, clk);
  D_Flip_Flop d_ff_1 (.D(or_In[0]), .clk(clk_t), .Q(out_16[0]), .reset(reset));  // open: Qn, preset
  D_Flip_Flop d_ff_2 (.D(or_In[1]), .clk(clk_t), .Q(out_16[1]), .reset(reset));  // open: Qn, preset
  D_Flip_Flop d_ff_3 (.D(or_In[2]), .clk(clk_t), .Q(out_16[2]), .reset(reset));  // open: Qn, preset
  D_Flip_Flop d_ff_4 (.D(or_In[3]), .clk(clk_t), .Q(out_16[3]), .reset(reset));  // open: Qn, preset
  D_Flip_Flop d_ff_5 (.D(or_In[4]), .clk(clk_t), .Q(out_16[4]), .reset(reset));  // open: Qn, preset
  D_Flip_Flop d_ff_6 (.D(or_In[5]), .clk(clk_t), .Q(out_16[5]), .reset(reset));  // open: Qn, preset
  D_Flip_Flop d_ff_7 (.D(or_In[6]), .clk(clk_t), .Q(out_16[6]), .reset(reset));  // open: Qn, preset
  D_Flip_Flop d_ff_8 (.D(or_In[7]), .clk(clk_t), .Q(out_16[7]), .reset(reset));  // open: Qn, preset
  D_Flip_Flop d_ff_9 (.D(or_In[8]), .clk(clk_t), .Q(out_16[8]), .reset(reset));  // open: Qn, preset
  D_Flip_Flop d_ff_10 (.D(or_In[9]), .clk(clk_t), .Q(out_16[9]), .reset(reset));  // open: Qn, preset
  D_Flip_Flop d_ff_11 (.D(or_In[10]), .clk(clk_t), .Q(out_16[10]), .reset(reset));  // open: Qn, preset
  D_Flip_Flop d_ff_12 (.D(or_In[11]), .clk(clk_t), .Q(out_16[11]), .reset(reset));  // open: Qn, preset
  D_Flip_Flop d_ff_13 (.D(or_In[12]), .clk(clk_t), .Q(out_16[12]), .reset(reset));  // open: Qn, preset
  D_Flip_Flop d_ff_14 (.D(or_In[13]), .clk(clk_t), .Q(out_16[13]), .reset(reset));  // open: Qn, preset
  D_Flip_Flop d_ff_15 (.D(or_In[14]), .clk(clk_t), .Q(out_16[14]), .reset(reset));  // open: Qn, preset
  D_Flip_Flop d_ff_16 (.D(or_In[15]), .clk(clk_t), .Q(out_16[15]), .reset(reset));  // open: Qn, preset
endmodule

module ALU (
  input  [15:0] InputData1,
  input  [15:0] InputData2,
  input  [3:0] shift,
  input  [2:0] OpType,
  output [15:0] lteq,
  output zero,
  output [15:0] OutputData
);

  wire [15:0] and_1_out, bitleftshift_1_leftout, bitrightshift_1_rightout, fulladder_1_result, not_1_out;

  fulladder fulladder_1 (.result(fulladder_1_result), .sub(1'b0), .B(InputData2), .A(InputData1));  // open: zero, ovf
  fulladder fulladder_2 (.result(lteq), .sub(1'b1), .B(InputData2), .A(InputData1), .zero(zero));  // open: ovf
  bitleftshift bitleftshift_1 (.blsinput(InputData1), .shiftamm(shift), .leftout(bitleftshift_1_leftout));
  bitrightshift bitrightshift_1 (.A(InputData1), .B(shift), .rightout(bitrightshift_1_rightout));
  assign not_1_out = ~InputData1;  // NOT_Gate not_1, 16 bits wide
  assign and_1_out = InputData1 & InputData2;  // AND_Gate and_1, 16 bits wide
  Multiplexer #(.select(3), .width(16), .enable("false")) multiplexer_1 (
    .in0(fulladder_1_result), .in1(lteq), .in2(bitleftshift_1_leftout), .in3(bitrightshift_1_rightout),
    .in4(not_1_out), .in5(and_1_out), .out(OutputData), .sel(OpType));  // open: in6, in7

  // Other names for the same wires on the sheet: amount[3:0] = shift; input1[15:0] = InputData1;
  //   input2[15:0] = InputData2

  // Notes on the sheet:
  //   sub = 000; add = 001; lsh = 010; rsh = 011; not = 100; AND = 101
endmodule

module fulladder (
  input  [15:0] B,
  input  [15:0] A,
  input  sub,
  output zero,
  output [15:0] result,
  output ovf
);

  wire adderbit_1_cout, adderbit_2_cout, adderbit_3_cout, adderbit_4_cout, adderbit_5_cout, adderbit_6_cout,
       adderbit_7_cout, adderbit_8_cout, adderbit_9_cout, adderbit_10_cout, adderbit_11_cout,
       adderbit_12_cout, adderbit_13_cout, adderbit_14_cout, adderbit_15_cout, adderbit_16_cout, xor_1_out,
       xor_2_out, xor_3_out, xor_4_out, xor_5_out, xor_6_out, xor_7_out, xor_8_out, xor_9_out, xor_10_out,
       xor_11_out, xor_12_out, xor_13_out, xor_14_out, xor_15_out, xor_16_out;

  xor xor_1 (xor_1_out, sub, B[15]);
  xor xor_2 (xor_2_out, sub, B[14]);
  xor xor_3 (xor_3_out, sub, B[13]);
  xor xor_4 (xor_4_out, sub, B[12]);
  xor xor_5 (xor_5_out, sub, B[11]);
  xor xor_6 (xor_6_out, sub, B[10]);
  xor xor_7 (xor_7_out, sub, B[9]);
  xor xor_8 (xor_8_out, sub, B[8]);
  xor xor_9 (xor_9_out, sub, B[7]);
  xor xor_10 (xor_10_out, sub, B[6]);
  xor xor_11 (xor_11_out, sub, B[5]);
  xor xor_12 (xor_12_out, sub, B[4]);
  xor xor_13 (xor_13_out, sub, B[3]);
  xor xor_14 (xor_14_out, sub, B[2]);
  xor xor_15 (xor_15_out, sub, B[1]);
  xor xor_16 (xor_16_out, sub, B[0]);
  adderbit adderbit_1 (.Cin(adderbit_2_cout), .A(A[15]), .B(xor_1_out), .Sum(result[15]), .Cout(adderbit_1_cout));
  adderbit adderbit_2 (.Cin(adderbit_3_cout), .A(A[14]), .B(xor_2_out), .Sum(result[14]), .Cout(adderbit_2_cout));
  adderbit adderbit_3 (.Cin(adderbit_4_cout), .A(A[13]), .B(xor_3_out), .Sum(result[13]), .Cout(adderbit_3_cout));
  adderbit adderbit_4 (.Cin(adderbit_5_cout), .A(A[12]), .B(xor_4_out), .Sum(result[12]), .Cout(adderbit_4_cout));
  adderbit adderbit_5 (.Cin(adderbit_6_cout), .A(A[11]), .B(xor_5_out), .Sum(result[11]), .Cout(adderbit_5_cout));
  adderbit adderbit_6 (.Cin(adderbit_7_cout), .A(A[10]), .B(xor_6_out), .Sum(result[10]), .Cout(adderbit_6_cout));
  adderbit adderbit_7 (.Cin(adderbit_8_cout), .A(A[9]), .B(xor_7_out), .Sum(result[9]), .Cout(adderbit_7_cout));
  adderbit adderbit_8 (.Cin(adderbit_9_cout), .A(A[8]), .B(xor_8_out), .Sum(result[8]), .Cout(adderbit_8_cout));
  adderbit adderbit_9 (.Cin(adderbit_10_cout), .A(A[7]), .B(xor_9_out), .Sum(result[7]), .Cout(adderbit_9_cout));
  adderbit adderbit_10 (.Cin(adderbit_11_cout), .A(A[6]), .B(xor_10_out), .Sum(result[6]), .Cout(adderbit_10_cout));
  adderbit adderbit_11 (.Cin(adderbit_12_cout), .A(A[5]), .B(xor_11_out), .Sum(result[5]), .Cout(adderbit_11_cout));
  adderbit adderbit_12 (.Cin(adderbit_13_cout), .A(A[4]), .B(xor_12_out), .Sum(result[4]), .Cout(adderbit_12_cout));
  adderbit adderbit_13 (.Cin(adderbit_14_cout), .A(A[3]), .B(xor_13_out), .Sum(result[3]), .Cout(adderbit_13_cout));
  adderbit adderbit_14 (.Cin(adderbit_15_cout), .A(A[2]), .B(xor_14_out), .Sum(result[2]), .Cout(adderbit_14_cout));
  adderbit adderbit_15 (.Cin(adderbit_16_cout), .A(A[1]), .B(xor_15_out), .Sum(result[1]), .Cout(adderbit_15_cout));
  adderbit adderbit_16 (.Cin(sub), .A(A[0]), .B(xor_16_out), .Sum(result[0]), .Cout(adderbit_16_cout));
  xor xor_17 (ovf, adderbit_2_cout, adderbit_1_cout);
  or or_1 (zero, result[15], result[14], result[13], result[12], result[11], result[10], result[9], result[8], result[6], result[5], result[4], result[3], result[2], result[1], result[0], result[7]);
endmodule

module adderbit (
  input  Cin,
  input  A,
  input  B,
  output Sum,
  output Cout
);

  wire and_1_out, and_2_out, xor_1_out;

  xor xor_1 (xor_1_out, A, B);
  and and_1 (and_1_out, A, B);
  and and_2 (and_2_out, xor_1_out, Cin);
  or or_1 (Cout, and_2_out, and_1_out);
  xor xor_2 (Sum, Cin, xor_1_out);
endmodule

module bitleftshift (
  input  [15:0] blsinput,
  input  [3:0] shiftamm,
  output [15:0] leftout
);

  wire multiplexer_1_out, multiplexer_2_out, multiplexer_3_out, multiplexer_4_out, multiplexer_5_out,
       multiplexer_6_out, multiplexer_7_out, multiplexer_8_out, multiplexer_9_out, multiplexer_10_out,
       multiplexer_11_out, multiplexer_12_out, multiplexer_13_out, multiplexer_14_out, multiplexer_15_out,
       multiplexer_16_out, multiplexer_17_out, multiplexer_18_out, multiplexer_19_out, multiplexer_20_out,
       multiplexer_21_out, multiplexer_22_out, multiplexer_23_out, multiplexer_24_out, multiplexer_25_out,
       multiplexer_26_out, multiplexer_27_out, multiplexer_28_out, multiplexer_29_out, multiplexer_30_out,
       multiplexer_31_out, multiplexer_32_out, multiplexer_33_out, multiplexer_34_out, multiplexer_35_out,
       multiplexer_36_out, multiplexer_37_out, multiplexer_38_out, multiplexer_39_out, multiplexer_40_out,
       multiplexer_41_out, multiplexer_42_out, multiplexer_43_out, multiplexer_44_out, multiplexer_45_out,
       multiplexer_46_out, multiplexer_47_out, multiplexer_48_out;

  Multiplexer #(.enable("false")) multiplexer_1 (
    .in0(blsinput[15]), .in1(blsinput[14]), .out(multiplexer_1_out), .sel(shiftamm[0]));
  Multiplexer #(.enable("false")) multiplexer_2 (
    .in0(blsinput[14]), .in1(blsinput[13]), .out(multiplexer_2_out), .sel(shiftamm[0]));
  Multiplexer #(.enable("false")) multiplexer_3 (
    .in0(blsinput[13]), .in1(blsinput[12]), .out(multiplexer_3_out), .sel(shiftamm[0]));
  Multiplexer #(.enable("false")) multiplexer_4 (
    .in0(blsinput[12]), .in1(blsinput[11]), .out(multiplexer_4_out), .sel(shiftamm[0]));
  Multiplexer #(.enable("false")) multiplexer_5 (
    .in0(blsinput[11]), .in1(blsinput[10]), .out(multiplexer_5_out), .sel(shiftamm[0]));
  Multiplexer #(.enable("false")) multiplexer_6 (
    .in0(blsinput[10]), .in1(blsinput[9]), .out(multiplexer_6_out), .sel(shiftamm[0]));
  Multiplexer #(.enable("false")) multiplexer_7 (
    .in0(blsinput[9]), .in1(blsinput[8]), .out(multiplexer_7_out), .sel(shiftamm[0]));
  Multiplexer #(.enable("false")) multiplexer_8 (
    .in0(blsinput[8]), .in1(blsinput[7]), .out(multiplexer_8_out), .sel(shiftamm[0]));
  Multiplexer #(.enable("false")) multiplexer_9 (
    .in0(blsinput[7]), .in1(blsinput[6]), .out(multiplexer_9_out), .sel(shiftamm[0]));
  Multiplexer #(.enable("false")) multiplexer_10 (
    .in0(blsinput[6]), .in1(blsinput[5]), .out(multiplexer_10_out), .sel(shiftamm[0]));
  Multiplexer #(.enable("false")) multiplexer_11 (
    .in0(blsinput[5]), .in1(blsinput[4]), .out(multiplexer_11_out), .sel(shiftamm[0]));
  Multiplexer #(.enable("false")) multiplexer_12 (
    .in0(blsinput[4]), .in1(blsinput[3]), .out(multiplexer_12_out), .sel(shiftamm[0]));
  Multiplexer #(.enable("false")) multiplexer_13 (
    .in0(blsinput[3]), .in1(blsinput[2]), .out(multiplexer_13_out), .sel(shiftamm[0]));
  Multiplexer #(.enable("false")) multiplexer_14 (
    .in0(blsinput[2]), .in1(blsinput[1]), .out(multiplexer_14_out), .sel(shiftamm[0]));
  Multiplexer #(.enable("false")) multiplexer_15 (
    .in0(blsinput[1]), .in1(blsinput[0]), .out(multiplexer_15_out), .sel(shiftamm[0]));
  Multiplexer #(.enable("false")) multiplexer_16 (
    .in0(blsinput[0]), .in1(1'b0), .out(multiplexer_16_out), .sel(shiftamm[0]));
  Multiplexer #(.enable("false")) multiplexer_17 (
    .in0(multiplexer_1_out), .in1(multiplexer_3_out), .out(multiplexer_17_out), .sel(shiftamm[1]));
  Multiplexer #(.enable("false")) multiplexer_18 (
    .in0(multiplexer_2_out), .in1(multiplexer_4_out), .out(multiplexer_18_out), .sel(shiftamm[1]));
  Multiplexer #(.enable("false")) multiplexer_19 (
    .in0(multiplexer_3_out), .in1(multiplexer_5_out), .out(multiplexer_19_out), .sel(shiftamm[1]));
  Multiplexer #(.enable("false")) multiplexer_20 (
    .in0(multiplexer_4_out), .in1(multiplexer_6_out), .out(multiplexer_20_out), .sel(shiftamm[1]));
  Multiplexer #(.enable("false")) multiplexer_21 (
    .in0(multiplexer_5_out), .in1(multiplexer_7_out), .out(multiplexer_21_out), .sel(shiftamm[1]));
  Multiplexer #(.enable("false")) multiplexer_22 (
    .in0(multiplexer_6_out), .in1(multiplexer_8_out), .out(multiplexer_22_out), .sel(shiftamm[1]));
  Multiplexer #(.enable("false")) multiplexer_23 (
    .in0(multiplexer_7_out), .in1(multiplexer_9_out), .out(multiplexer_23_out), .sel(shiftamm[1]));
  Multiplexer #(.enable("false")) multiplexer_24 (
    .in0(multiplexer_8_out), .in1(multiplexer_10_out), .out(multiplexer_24_out), .sel(shiftamm[1]));
  Multiplexer #(.enable("false")) multiplexer_25 (
    .in0(multiplexer_9_out), .in1(multiplexer_11_out), .out(multiplexer_25_out), .sel(shiftamm[1]));
  Multiplexer #(.enable("false")) multiplexer_26 (
    .in0(multiplexer_10_out), .in1(multiplexer_12_out), .out(multiplexer_26_out), .sel(shiftamm[1]));
  Multiplexer #(.enable("false")) multiplexer_27 (
    .in0(multiplexer_11_out), .in1(multiplexer_13_out), .out(multiplexer_27_out), .sel(shiftamm[1]));
  Multiplexer #(.enable("false")) multiplexer_28 (
    .in0(multiplexer_12_out), .in1(multiplexer_14_out), .out(multiplexer_28_out), .sel(shiftamm[1]));
  Multiplexer #(.enable("false")) multiplexer_29 (
    .in0(multiplexer_13_out), .in1(multiplexer_15_out), .out(multiplexer_29_out), .sel(shiftamm[1]));
  Multiplexer #(.enable("false")) multiplexer_30 (
    .in0(multiplexer_14_out), .in1(multiplexer_16_out), .out(multiplexer_30_out), .sel(shiftamm[1]));
  Multiplexer #(.enable("false")) multiplexer_31 (
    .in0(multiplexer_15_out), .in1(1'b0), .out(multiplexer_31_out), .sel(shiftamm[1]));
  Multiplexer #(.enable("false")) multiplexer_32 (
    .in0(multiplexer_16_out), .in1(1'b0), .out(multiplexer_32_out), .sel(shiftamm[1]));
  Multiplexer #(.enable("false")) multiplexer_33 (
    .in0(multiplexer_17_out), .in1(multiplexer_21_out), .out(multiplexer_33_out), .sel(shiftamm[2]));
  Multiplexer #(.enable("false")) multiplexer_34 (
    .in0(multiplexer_18_out), .in1(multiplexer_22_out), .out(multiplexer_34_out), .sel(shiftamm[2]));
  Multiplexer #(.enable("false")) multiplexer_35 (
    .in0(multiplexer_19_out), .in1(multiplexer_23_out), .out(multiplexer_35_out), .sel(shiftamm[2]));
  Multiplexer #(.enable("false")) multiplexer_36 (
    .in0(multiplexer_20_out), .in1(multiplexer_24_out), .out(multiplexer_36_out), .sel(shiftamm[2]));
  Multiplexer #(.enable("false")) multiplexer_37 (
    .in0(multiplexer_21_out), .in1(multiplexer_25_out), .out(multiplexer_37_out), .sel(shiftamm[2]));
  Multiplexer #(.enable("false")) multiplexer_38 (
    .in0(multiplexer_22_out), .in1(multiplexer_26_out), .out(multiplexer_38_out), .sel(shiftamm[2]));
  Multiplexer #(.enable("false")) multiplexer_39 (
    .in0(multiplexer_23_out), .in1(multiplexer_27_out), .out(multiplexer_39_out), .sel(shiftamm[2]));
  Multiplexer #(.enable("false")) multiplexer_40 (
    .in0(multiplexer_24_out), .in1(multiplexer_28_out), .out(multiplexer_40_out), .sel(shiftamm[2]));
  Multiplexer #(.enable("false")) multiplexer_41 (
    .in0(multiplexer_25_out), .in1(multiplexer_29_out), .out(multiplexer_41_out), .sel(shiftamm[2]));
  Multiplexer #(.enable("false")) multiplexer_42 (
    .in0(multiplexer_26_out), .in1(multiplexer_30_out), .out(multiplexer_42_out), .sel(shiftamm[2]));
  Multiplexer #(.enable("false")) multiplexer_43 (
    .in0(multiplexer_27_out), .in1(multiplexer_31_out), .out(multiplexer_43_out), .sel(shiftamm[2]));
  Multiplexer #(.enable("false")) multiplexer_44 (
    .in0(multiplexer_28_out), .in1(multiplexer_32_out), .out(multiplexer_44_out), .sel(shiftamm[2]));
  Multiplexer #(.enable("false")) multiplexer_45 (
    .in0(multiplexer_29_out), .in1(1'b0), .out(multiplexer_45_out), .sel(shiftamm[2]));
  Multiplexer #(.enable("false")) multiplexer_46 (
    .in0(multiplexer_30_out), .in1(1'b0), .out(multiplexer_46_out), .sel(shiftamm[2]));
  Multiplexer #(.enable("false")) multiplexer_47 (
    .in0(multiplexer_31_out), .in1(1'b0), .out(multiplexer_47_out), .sel(shiftamm[2]));
  Multiplexer #(.enable("false")) multiplexer_48 (
    .in0(multiplexer_32_out), .in1(1'b0), .out(multiplexer_48_out), .sel(shiftamm[2]));
  Multiplexer #(.enable("false")) multiplexer_49 (
    .in0(multiplexer_33_out), .in1(multiplexer_41_out), .out(leftout[15]), .sel(shiftamm[3]));
  Multiplexer #(.enable("false")) multiplexer_50 (
    .in0(multiplexer_34_out), .in1(multiplexer_42_out), .out(leftout[14]), .sel(shiftamm[3]));
  Multiplexer #(.enable("false")) multiplexer_51 (
    .in0(multiplexer_35_out), .in1(multiplexer_43_out), .out(leftout[13]), .sel(shiftamm[3]));
  Multiplexer #(.enable("false")) multiplexer_52 (
    .in0(multiplexer_36_out), .in1(multiplexer_44_out), .out(leftout[12]), .sel(shiftamm[3]));
  Multiplexer #(.enable("false")) multiplexer_53 (
    .in0(multiplexer_37_out), .in1(multiplexer_45_out), .out(leftout[11]), .sel(shiftamm[3]));
  Multiplexer #(.enable("false")) multiplexer_54 (
    .in0(multiplexer_38_out), .in1(multiplexer_46_out), .out(leftout[10]), .sel(shiftamm[3]));
  Multiplexer #(.enable("false")) multiplexer_55 (
    .in0(multiplexer_39_out), .in1(multiplexer_47_out), .out(leftout[9]), .sel(shiftamm[3]));
  Multiplexer #(.enable("false")) multiplexer_56 (
    .in0(multiplexer_40_out), .in1(multiplexer_48_out), .out(leftout[8]), .sel(shiftamm[3]));
  Multiplexer #(.enable("false")) multiplexer_57 (
    .in0(multiplexer_41_out), .in1(1'b0), .out(leftout[7]), .sel(shiftamm[3]));
  Multiplexer #(.enable("false")) multiplexer_58 (
    .in0(multiplexer_42_out), .in1(1'b0), .out(leftout[6]), .sel(shiftamm[3]));
  Multiplexer #(.enable("false")) multiplexer_59 (
    .in0(multiplexer_43_out), .in1(1'b0), .out(leftout[5]), .sel(shiftamm[3]));
  Multiplexer #(.enable("false")) multiplexer_60 (
    .in0(multiplexer_44_out), .in1(1'b0), .out(leftout[4]), .sel(shiftamm[3]));
  Multiplexer #(.enable("false")) multiplexer_61 (
    .in0(multiplexer_45_out), .in1(1'b0), .out(leftout[3]), .sel(shiftamm[3]));
  Multiplexer #(.enable("false")) multiplexer_62 (
    .in0(multiplexer_46_out), .in1(1'b0), .out(leftout[2]), .sel(shiftamm[3]));
  Multiplexer #(.enable("false")) multiplexer_63 (
    .in0(multiplexer_47_out), .in1(1'b0), .out(leftout[1]), .sel(shiftamm[3]));
  Multiplexer #(.enable("false")) multiplexer_64 (
    .in0(multiplexer_48_out), .in1(1'b0), .out(leftout[0]), .sel(shiftamm[3]));

  // Other names for the same wires on the sheet: b0 = blsinput[0]; b1 = blsinput[1]; b2 = blsinput[2];
  //   b3 = blsinput[3]; b4 = blsinput[4]; b5 = blsinput[5]; b6 = blsinput[6]; b7 = blsinput[7]; b8 = blsinput[8];
  //   b9 = blsinput[9]; b10 = blsinput[10]; b11 = blsinput[11]; b12 = blsinput[12]; b13 = blsinput[13];
  //   b14 = blsinput[14]; b15 = blsinput[15]; o0 = leftout[0]; o1 = leftout[1]; o2 = leftout[2]; o3 = leftout[3];
  //   o4 = leftout[4]; o5 = leftout[5]; o6 = leftout[6]; o7 = leftout[7]; o8 = leftout[8]; o9 = leftout[9];
  //   o10 = leftout[10]; o11 = leftout[11]; o12 = leftout[12]; o13 = leftout[13]; o14 = leftout[14];
  //   o15 = leftout[15]; shift3 = shiftamm[0]; shift2 = shiftamm[1]; shift1 = shiftamm[2]; shift0 = shiftamm[3]
endmodule

module memorylatch (
  input  [15:0] address,
  input  WE,
  input  clk,
  input  [15:0] data_in,
  output [15:0] address_latched,
  output WE_latched,
  output OE_latched,
  output [15:0] data_in_latched
);

  wire DMwe_latch_q;
  wire [15:0] addr_latch_q;

  Register #(.width(16), .trigger("falling")) addr_latch (
    .D(address), .en(WE), .clk(clk), .Q(addr_latch_q));  // open: clr
  D_Flip_Flop #(.trigger("falling")) DMwe_latch (.D(WE), .clk(clk), .Q(DMwe_latch_q));  // open: Qn, preset, reset
  Register #(.width(16), .trigger("falling")) data_to_be_written (
    .D(data_in), .en(WE), .clk(clk), .Q(data_in_latched));  // open: clr
  Multiplexer #(.width(16), .enable("false")) multiplexer_1 (
    .in0(address), .in1(addr_latch_q), .out(address_latched), .sel(DMwe_latch_q));
  and and_1 (WE_latched, clk, DMwe_latch_q);
  not not_1 (OE_latched, WE_latched);
endmodule

module bitrightshift (
  input  [15:0] A,
  input  [3:0] B,
  output [15:0] rightout
);

  wire multiplexer_1_out, multiplexer_2_out, multiplexer_3_out, multiplexer_4_out, multiplexer_5_out,
       multiplexer_6_out, multiplexer_7_out, multiplexer_8_out, multiplexer_9_out, multiplexer_10_out,
       multiplexer_11_out, multiplexer_12_out, multiplexer_13_out, multiplexer_14_out, multiplexer_15_out,
       multiplexer_16_out, multiplexer_17_out, multiplexer_18_out, multiplexer_19_out, multiplexer_20_out,
       multiplexer_21_out, multiplexer_22_out, multiplexer_23_out, multiplexer_24_out, multiplexer_25_out,
       multiplexer_26_out, multiplexer_27_out, multiplexer_28_out, multiplexer_29_out, multiplexer_30_out,
       multiplexer_31_out, multiplexer_32_out, multiplexer_33_out, multiplexer_34_out, multiplexer_35_out,
       multiplexer_36_out, multiplexer_37_out, multiplexer_38_out, multiplexer_39_out, multiplexer_40_out,
       multiplexer_41_out, multiplexer_42_out, multiplexer_43_out, multiplexer_44_out, multiplexer_45_out,
       multiplexer_46_out, multiplexer_47_out, multiplexer_48_out;

  Multiplexer #(.enable("false")) multiplexer_1 (.in0(A[0]), .in1(A[1]), .out(multiplexer_1_out), .sel(B[0]));
  Multiplexer #(.enable("false")) multiplexer_2 (.in0(A[1]), .in1(A[2]), .out(multiplexer_2_out), .sel(B[0]));
  Multiplexer #(.enable("false")) multiplexer_3 (.in0(A[2]), .in1(A[3]), .out(multiplexer_3_out), .sel(B[0]));
  Multiplexer #(.enable("false")) multiplexer_4 (.in0(A[3]), .in1(A[4]), .out(multiplexer_4_out), .sel(B[0]));
  Multiplexer #(.enable("false")) multiplexer_5 (.in0(A[4]), .in1(A[5]), .out(multiplexer_5_out), .sel(B[0]));
  Multiplexer #(.enable("false")) multiplexer_6 (.in0(A[5]), .in1(A[6]), .out(multiplexer_6_out), .sel(B[0]));
  Multiplexer #(.enable("false")) multiplexer_7 (.in0(A[6]), .in1(A[7]), .out(multiplexer_7_out), .sel(B[0]));
  Multiplexer #(.enable("false")) multiplexer_8 (.in0(A[7]), .in1(A[8]), .out(multiplexer_8_out), .sel(B[0]));
  Multiplexer #(.enable("false")) multiplexer_9 (.in0(A[8]), .in1(A[9]), .out(multiplexer_9_out), .sel(B[0]));
  Multiplexer #(.enable("false")) multiplexer_10 (.in0(A[9]), .in1(A[10]), .out(multiplexer_10_out), .sel(B[0]));
  Multiplexer #(.enable("false")) multiplexer_11 (.in0(A[10]), .in1(A[11]), .out(multiplexer_11_out), .sel(B[0]));
  Multiplexer #(.enable("false")) multiplexer_12 (.in0(A[11]), .in1(A[12]), .out(multiplexer_12_out), .sel(B[0]));
  Multiplexer #(.enable("false")) multiplexer_13 (.in0(A[12]), .in1(A[13]), .out(multiplexer_13_out), .sel(B[0]));
  Multiplexer #(.enable("false")) multiplexer_14 (.in0(A[13]), .in1(A[14]), .out(multiplexer_14_out), .sel(B[0]));
  Multiplexer #(.enable("false")) multiplexer_15 (.in0(A[14]), .in1(A[15]), .out(multiplexer_15_out), .sel(B[0]));
  Multiplexer #(.enable("false")) multiplexer_16 (.in0(A[15]), .in1(1'b0), .out(multiplexer_16_out), .sel(B[0]));
  Multiplexer #(.enable("false")) multiplexer_17 (
    .in0(multiplexer_1_out), .in1(multiplexer_3_out), .out(multiplexer_17_out), .sel(B[1]));
  Multiplexer #(.enable("false")) multiplexer_18 (
    .in0(multiplexer_2_out), .in1(multiplexer_4_out), .out(multiplexer_18_out), .sel(B[1]));
  Multiplexer #(.enable("false")) multiplexer_19 (
    .in0(multiplexer_3_out), .in1(multiplexer_5_out), .out(multiplexer_19_out), .sel(B[1]));
  Multiplexer #(.enable("false")) multiplexer_20 (
    .in0(multiplexer_4_out), .in1(multiplexer_6_out), .out(multiplexer_20_out), .sel(B[1]));
  Multiplexer #(.enable("false")) multiplexer_21 (
    .in0(multiplexer_5_out), .in1(multiplexer_7_out), .out(multiplexer_21_out), .sel(B[1]));
  Multiplexer #(.enable("false")) multiplexer_22 (
    .in0(multiplexer_6_out), .in1(multiplexer_8_out), .out(multiplexer_22_out), .sel(B[1]));
  Multiplexer #(.enable("false")) multiplexer_23 (
    .in0(multiplexer_7_out), .in1(multiplexer_9_out), .out(multiplexer_23_out), .sel(B[1]));
  Multiplexer #(.enable("false")) multiplexer_24 (
    .in0(multiplexer_8_out), .in1(multiplexer_10_out), .out(multiplexer_24_out), .sel(B[1]));
  Multiplexer #(.enable("false")) multiplexer_25 (
    .in0(multiplexer_9_out), .in1(multiplexer_11_out), .out(multiplexer_25_out), .sel(B[1]));
  Multiplexer #(.enable("false")) multiplexer_26 (
    .in0(multiplexer_10_out), .in1(multiplexer_12_out), .out(multiplexer_26_out), .sel(B[1]));
  Multiplexer #(.enable("false")) multiplexer_27 (
    .in0(multiplexer_11_out), .in1(multiplexer_13_out), .out(multiplexer_27_out), .sel(B[1]));
  Multiplexer #(.enable("false")) multiplexer_28 (
    .in0(multiplexer_12_out), .in1(multiplexer_14_out), .out(multiplexer_28_out), .sel(B[1]));
  Multiplexer #(.enable("false")) multiplexer_29 (
    .in0(multiplexer_13_out), .in1(multiplexer_15_out), .out(multiplexer_29_out), .sel(B[1]));
  Multiplexer #(.enable("false")) multiplexer_30 (
    .in0(multiplexer_14_out), .in1(multiplexer_16_out), .out(multiplexer_30_out), .sel(B[1]));
  Multiplexer #(.enable("false")) multiplexer_31 (
    .in0(multiplexer_15_out), .in1(1'b0), .out(multiplexer_31_out), .sel(B[1]));
  Multiplexer #(.enable("false")) multiplexer_32 (
    .in0(multiplexer_16_out), .in1(1'b0), .out(multiplexer_32_out), .sel(B[1]));
  Multiplexer #(.enable("false")) multiplexer_33 (
    .in0(multiplexer_17_out), .in1(multiplexer_21_out), .out(multiplexer_33_out), .sel(B[2]));
  Multiplexer #(.enable("false")) multiplexer_34 (
    .in0(multiplexer_18_out), .in1(multiplexer_22_out), .out(multiplexer_34_out), .sel(B[2]));
  Multiplexer #(.enable("false")) multiplexer_35 (
    .in0(multiplexer_19_out), .in1(multiplexer_23_out), .out(multiplexer_35_out), .sel(B[2]));
  Multiplexer #(.enable("false")) multiplexer_36 (
    .in0(multiplexer_20_out), .in1(multiplexer_24_out), .out(multiplexer_36_out), .sel(B[2]));
  Multiplexer #(.enable("false")) multiplexer_37 (
    .in0(multiplexer_21_out), .in1(multiplexer_25_out), .out(multiplexer_37_out), .sel(B[2]));
  Multiplexer #(.enable("false")) multiplexer_38 (
    .in0(multiplexer_22_out), .in1(multiplexer_26_out), .out(multiplexer_38_out), .sel(B[2]));
  Multiplexer #(.enable("false")) multiplexer_39 (
    .in0(multiplexer_23_out), .in1(multiplexer_27_out), .out(multiplexer_39_out), .sel(B[2]));
  Multiplexer #(.enable("false")) multiplexer_40 (
    .in0(multiplexer_24_out), .in1(multiplexer_28_out), .out(multiplexer_40_out), .sel(B[2]));
  Multiplexer #(.enable("false")) multiplexer_41 (
    .in0(multiplexer_25_out), .in1(multiplexer_29_out), .out(multiplexer_41_out), .sel(B[2]));
  Multiplexer #(.enable("false")) multiplexer_42 (
    .in0(multiplexer_26_out), .in1(multiplexer_30_out), .out(multiplexer_42_out), .sel(B[2]));
  Multiplexer #(.enable("false")) multiplexer_43 (
    .in0(multiplexer_27_out), .in1(multiplexer_31_out), .out(multiplexer_43_out), .sel(B[2]));
  Multiplexer #(.enable("false")) multiplexer_44 (
    .in0(multiplexer_28_out), .in1(multiplexer_32_out), .out(multiplexer_44_out), .sel(B[2]));
  Multiplexer #(.enable("false")) multiplexer_45 (
    .in0(multiplexer_29_out), .in1(1'b0), .out(multiplexer_45_out), .sel(B[2]));
  Multiplexer #(.enable("false")) multiplexer_46 (
    .in0(multiplexer_30_out), .in1(1'b0), .out(multiplexer_46_out), .sel(B[2]));
  Multiplexer #(.enable("false")) multiplexer_47 (
    .in0(multiplexer_31_out), .in1(1'b0), .out(multiplexer_47_out), .sel(B[2]));
  Multiplexer #(.enable("false")) multiplexer_48 (
    .in0(multiplexer_32_out), .in1(1'b0), .out(multiplexer_48_out), .sel(B[2]));
  Multiplexer #(.enable("false")) multiplexer_49 (
    .in0(multiplexer_33_out), .in1(multiplexer_41_out), .out(rightout[0]), .sel(B[3]));
  Multiplexer #(.enable("false")) multiplexer_50 (
    .in0(multiplexer_34_out), .in1(multiplexer_42_out), .out(rightout[1]), .sel(B[3]));
  Multiplexer #(.enable("false")) multiplexer_51 (
    .in0(multiplexer_35_out), .in1(multiplexer_43_out), .out(rightout[2]), .sel(B[3]));
  Multiplexer #(.enable("false")) multiplexer_52 (
    .in0(multiplexer_36_out), .in1(multiplexer_44_out), .out(rightout[3]), .sel(B[3]));
  Multiplexer #(.enable("false")) multiplexer_53 (
    .in0(multiplexer_37_out), .in1(multiplexer_45_out), .out(rightout[4]), .sel(B[3]));
  Multiplexer #(.enable("false")) multiplexer_54 (
    .in0(multiplexer_38_out), .in1(multiplexer_46_out), .out(rightout[5]), .sel(B[3]));
  Multiplexer #(.enable("false")) multiplexer_55 (
    .in0(multiplexer_39_out), .in1(multiplexer_47_out), .out(rightout[6]), .sel(B[3]));
  Multiplexer #(.enable("false")) multiplexer_56 (
    .in0(multiplexer_40_out), .in1(multiplexer_48_out), .out(rightout[7]), .sel(B[3]));
  Multiplexer #(.enable("false")) multiplexer_57 (.in0(multiplexer_41_out), .in1(1'b0), .out(rightout[8]), .sel(B[3]));
  Multiplexer #(.enable("false")) multiplexer_58 (.in0(multiplexer_42_out), .in1(1'b0), .out(rightout[9]), .sel(B[3]));
  Multiplexer #(.enable("false")) multiplexer_59 (.in0(multiplexer_43_out), .in1(1'b0), .out(rightout[10]), .sel(B[3]));
  Multiplexer #(.enable("false")) multiplexer_60 (.in0(multiplexer_44_out), .in1(1'b0), .out(rightout[11]), .sel(B[3]));
  Multiplexer #(.enable("false")) multiplexer_61 (.in0(multiplexer_45_out), .in1(1'b0), .out(rightout[12]), .sel(B[3]));
  Multiplexer #(.enable("false")) multiplexer_62 (.in0(multiplexer_46_out), .in1(1'b0), .out(rightout[13]), .sel(B[3]));
  Multiplexer #(.enable("false")) multiplexer_63 (.in0(multiplexer_47_out), .in1(1'b0), .out(rightout[14]), .sel(B[3]));
  Multiplexer #(.enable("false")) multiplexer_64 (.in0(multiplexer_48_out), .in1(1'b0), .out(rightout[15]), .sel(B[3]));

  // Other names for the same wires on the sheet: b0 = A[0]; b1 = A[1]; b2 = A[2]; b3 = A[3]; b4 = A[4]; b5 = A[5];
  //   b6 = A[6]; b7 = A[7]; b8 = A[8]; b9 = A[9]; b10 = A[10]; b11 = A[11]; b12 = A[12]; b13 = A[13]; b14 = A[14];
  //   b15 = A[15]; shift3 = B[0]; shift2 = B[1]; shift1 = B[2]; shift0 = B[3]; out0 = rightout[0]; out1 = rightout[1];
  //   out2 = rightout[2]; out3 = rightout[3]; out4 = rightout[4]; out5 = rightout[5]; out6 = rightout[6];
  //   out7 = rightout[7]; out8 = rightout[8]; out9 = rightout[9]; out10 = rightout[10]; out11 = rightout[11];
  //   out12 = rightout[12]; out13 = rightout[13]; out14 = rightout[14]; out15 = rightout[15]
endmodule
